# Fritzing sketch udmiduino-circuit (saved by Fritzing 0.9.4)
breadboards: 1

parts:
  Part1 = Arduino Uno (Rev3)
  S1 = Pushbutton [package="[SMD]"]
  R1 = Resistor [tolerance=±5% resistance=10k package="0402 [SMD]"]
  LED1 = LEDs [package=led10mm]
  LED2 = LEDs [package=led10mm]
  LED3 = LEDs [package=led10mm]

nets:
  N1: Part1.A0, LED1.C
  N2: Part1.D2, R1.Pin_1
  N3: Part1.D3_PWM, LED2.C
  N4: Part1.D5_PWM, LED3.C
  N5: Part1.GND, S1.Pin_1, S1.Pin_2, S1.Pin_3, S1.Pin_4, R1.Pin_0, LED1.A, LED2.A, LED3.A

notes:
  Reversed polarity! "lux_level"
  "dimmer_value"
  "lum_value"
